// Logisim project Assignment-1(qs1-a).circ as structural Verilog: 1 circuit, main circuit main
module main (
  input  X,
  input  Y,
  input  Z
);

  wire and_1_out, and_2_out, and_3_out, not_1_out, not_2_out, not_3_out, or_1_out;

  not not_1 (not_1_out, X);
  not not_2 (not_2_out, Y);
  not not_3 (not_3_out, Z);
  and and_1 (and_1_out, X, Y);
  and and_2 (and_2_out, not_1_out, Y, Z);
  and and_3 (and_3_out, not_2_out, not_3_out);
  or or_1 (or_1_out, and_1_out, and_2_out, and_3_out);
  LED led_1 (.in(or_1_out));

  // Notes on the sheet:
  //   QS: 1(b)
  //   XY
  //   X'YZ
  //   Y'Z'
  //   M
  //   Najifa Tabassum
  //   2211578042
endmodule
