// Logisim project Assignment-1(qs3).circ as structural Verilog: 1 circuit, main circuit main
module main (
  input  A,
  input  B,
  input  C
);

  wire and_1_out, and_2_out, not_1_out, not_2_out, or_1_out;

  not not_1 (not_1_out, A);
  not not_2 (not_2_out, B);
  and and_1 (and_1_out, not_2_out, C);
  and and_2 (and_2_out, A, C);
  or or_1 (or_1_out, not_1_out, and_1_out, and_2_out);
  LED led_1 (.in(or_1_out));

  // Notes on the sheet:
  //   QS: 3(a)
  //   A'
  //   B'C
  //   AC
  //   P
  //   Najifa Tabassum
  //   2211578042
endmodule
