// Logisim project FINALDRAFT.circ as structural Verilog: 2 circuits, main circuit main
module main (
  output C,
  output B,
  output a
);

  wire and_1_out, and_2_out, and_3_out, and_4_out, and_5_out, bcd_1_a, bcd_1_b, bcd_1_c, bcd_1_d, bcd_1_e,
       bcd_1_f, bcd_1_g, CLK_out, j_k_ff_1_qn, j_k_ff_2_qn, j_k_ff_3_qn, or_1_out, or_2_out;

  Clock CLK (.out(CLK_out));
  and and_1 (and_1_out, j_k_ff_1_qn, B, a);
  and and_2 (and_2_out, B, j_k_ff_3_qn);
  J_K_Flip_Flop j_k_ff_1 (.J(and_1_out), .K(and_2_out), .clk(CLK_out), .Q(C), .Qn(j_k_ff_1_qn));  // open: preset, reset
  and and_3 (and_3_out, j_k_ff_1_qn, a);
  and and_4 (and_4_out, C, j_k_ff_3_qn);
  or or_1 (or_1_out, and_3_out, and_4_out);
  or or_2 (or_2_out, j_k_ff_2_qn, j_k_ff_1_qn);
  and and_5 (and_5_out, j_k_ff_2_qn, a);
  J_K_Flip_Flop j_k_ff_2 (.J(and_5_out), .K(or_1_out), .clk(CLK_out), .Q(B), .Qn(j_k_ff_2_qn));  // open: preset, reset
  J_K_Flip_Flop j_k_ff_3 (.J(or_2_out), .K(or_2_out), .clk(CLK_out), .Q(a), .Qn(j_k_ff_3_qn));  // open: preset, reset
  BCD bcd_1 (
    .in_1(C), .in_2(B), .in_3(a), .a(bcd_1_a), .b(bcd_1_b), .c(bcd_1_c), .d(bcd_1_d), .e(bcd_1_e),
    .f(bcd_1_f), .g(bcd_1_g));
  _7_Segment_Display u_7_segment_display_1 (
    .g(bcd_1_g), .f(bcd_1_f), .a(bcd_1_a), .b(bcd_1_b), .e(bcd_1_e), .d(bcd_1_d), .c(bcd_1_c));  // open: dp

  // Notes on the sheet:
  //   C'BA
  //   BA'
  //   Jc
  //   B'+C'
  //   B'A
  //   C'A+CA'
  //   JB
  //   B'+C'
  //   JA
  //   C
  //   B
  //   A
endmodule

module BCD (
  input  in_1,
  input  in_2,
  input  in_3,
  output a,
  output b,
  output c,
  output d,
  output e,
  output f,
  output g
);

  wire and_1_out, and_2_out, and_3_out, and_4_out, and_5_out, and_6_out, and_7_out, and_8_out, and_9_out,
       not_1_out, not_2_out, not_3_out;

  not not_1 (not_1_out, in_1);
  not not_2 (not_2_out, in_2);
  not not_3 (not_3_out, in_3);
  or or_1 (a, not_2_out, in_1);
  or or_2 (b, not_1_out, in_3, in_2);
  or or_3 (c, in_2, in_1);
  and and_1 (and_1_out, not_1_out, not_2_out);
  and and_2 (and_2_out, in_1, in_2);
  or or_4 (d, and_1_out, and_2_out, and_3_out);
  and and_3 (and_3_out, not_2_out, not_3_out);
  and and_4 (and_4_out, not_1_out, not_2_out);
  or or_5 (e, and_4_out, and_5_out);
  and and_5 (and_5_out, in_1, in_2);
  and and_6 (and_6_out, in_1, not_3_out);
  or or_6 (f, and_6_out, and_7_out);
  and and_7 (and_7_out, in_1, in_2);
  and and_8 (and_8_out, not_1_out, not_2_out);
  or or_7 (g, and_8_out, and_9_out);
  and and_9 (and_9_out, in_1, not_3_out);
endmodule
