// Logisim project IDDisplay.circ as structural Verilog: 3 circuits, main circuit main
module main (
  input  C,
  input  B,
  input  A,
  input  C_2,
  input  B_2,
  input  A_2
);

  wire bcd_1_a, bcd_1_b, bcd_1_c, bcd_1_d, bcd_1_e, bcd_1_f, bcd_1_g, project_1_a, project_1_b, project_1_c,
       project_1_d, project_1_e, project_1_f, project_1_g;

  BCD bcd_1 (
    .h(C), .x2(B), .x3(A), .a(bcd_1_a), .b(bcd_1_b), .c(bcd_1_c), .d(bcd_1_d), .e(bcd_1_e), .f(bcd_1_f),
    .g(bcd_1_g));
  project project_1 (
    .h(C_2), .x2(B_2), .x3(A_2), .a(project_1_a), .b(project_1_b), .c(project_1_c), .d(project_1_d),
    .e(project_1_e), .f(project_1_f), .g(project_1_g));
  _7_Segment_Display u_7_segment_display_1 (
    .g(bcd_1_g), .f(bcd_1_f), .a(bcd_1_a), .b(bcd_1_b), .e(bcd_1_e), .d(bcd_1_d), .c(bcd_1_c));  // open: dp
  _7_Segment_Display u_7_segment_display_2 (
    .g(project_1_g), .f(project_1_f), .a(project_1_a), .b(project_1_b), .e(project_1_e), .d(project_1_d),
    .c(project_1_c));  // open: dp
endmodule

module BCD (
  input  h,
  input  x2,
  input  x3,
  output a,
  output b,
  output c,
  output d,
  output e,
  output f,
  output g
);

  wire nand_1_out, nand_2_out, nand_3_out, nand_7_out, nand_8_out, nand_9_out, nand_10_out, nand_11_out,
       nand_12_out, nand_13_out, nand_14_out, nand_15_out;

  nand nand_1 (nand_1_out, 1'b1, h);
  nand nand_2 (nand_2_out, 1'b1, x2);
  nand nand_3 (nand_3_out, 1'b1, x3);
  nand nand_4 (a, x2, nand_1_out);
  nand nand_5 (b, h, nand_3_out, nand_2_out);
  nand nand_6 (c, nand_2_out, nand_1_out);
  nand nand_7 (nand_7_out, nand_1_out, nand_2_out);
  nand nand_8 (nand_8_out, h, x2);
  nand nand_9 (nand_9_out, nand_2_out, nand_3_out);
  nand nand_10 (nand_10_out, nand_1_out, nand_2_out);
  nand nand_11 (nand_11_out, h, x2);
  nand nand_12 (nand_12_out, h, nand_3_out);
  nand nand_13 (nand_13_out, h, x2);
  nand nand_14 (nand_14_out, nand_1_out, nand_2_out);
  nand nand_15 (nand_15_out, h, nand_3_out);
  nand nand_16 (d, nand_7_out, nand_8_out, nand_9_out);
  nand nand_17 (e, nand_10_out, nand_11_out);
  nand nand_18 (f, nand_12_out, nand_13_out);
  nand nand_19 (g, nand_14_out, nand_15_out);
endmodule

module project (
  input  h,
  input  x2,
  input  x3,
  output a,
  output b,
  output c,
  output d,
  output e,
  output f,
  output g
);

  wire nand_1_out, nand_2_out, nand_3_out, nand_7_out, nand_8_out, nand_9_out, nand_10_out, nand_11_out,
       nand_12_out, nand_13_out, nand_14_out, nand_15_out;

  nand nand_1 (nand_1_out, 1'b1, h);
  nand nand_2 (nand_2_out, 1'b1, x2);
  nand nand_3 (nand_3_out, 1'b1, x3);
  nand nand_4 (a, x2, nand_1_out);
  nand nand_5 (b, h, nand_3_out, nand_2_out);
  nand nand_6 (c, nand_2_out, nand_1_out);
  nand nand_7 (nand_7_out, nand_1_out, nand_2_out);
  nand nand_8 (nand_8_out, h, x2);
  nand nand_9 (nand_9_out, nand_2_out, nand_3_out);
  nand nand_10 (nand_10_out, nand_1_out, nand_2_out);
  nand nand_11 (nand_11_out, h, x2);
  nand nand_12 (nand_12_out, h, nand_3_out);
  nand nand_13 (nand_13_out, h, x2);
  nand nand_14 (nand_14_out, nand_1_out, nand_2_out);
  nand nand_15 (nand_15_out, h, nand_3_out);
  nand nand_16 (d, nand_7_out, nand_8_out, nand_9_out);
  nand nand_17 (e, nand_10_out, nand_11_out);
  nand nand_18 (f, nand_12_out, nand_13_out);
  nand nand_19 (g, nand_14_out, nand_15_out);
endmodule
