// Logisim project Lab1.circ as structural Verilog: 1 circuit, main circuit main
module main (
  input  A,
  input  B,
  input  C
);

  wire and_1_out, and_2_out, and_3_out, not_1_out, not_2_out, or_1_out, or_2_out;

  not not_1 (not_1_out, A);
  not not_2 (not_2_out, B);
  and and_1 (and_1_out, not_1_out, C);
  and and_2 (and_2_out, A, not_2_out);
  and and_3 (and_3_out, B, C);
  or or_1 (or_1_out, and_1_out, and_2_out);
  or or_2 (or_2_out, or_1_out, and_3_out);
  LED A_prime_B_AB_prime_BC (.in(or_2_out));

  // Notes on the sheet:
  //   A'B
  //   AB'
  //   BC
  //   Najifa Tabassum
  //   2211578042
  //   Lab01
endmodule
