// Logisim project Lab2(max).circ as structural Verilog: 1 circuit, main circuit main
module main (
  input  A,
  input  B,
  input  C
);

  wire and_1_out, not_1_out, not_2_out, not_3_out, not_4_out, not_5_out, not_6_out, not_7_out, not_8_out,
       or_1_out, or_2_out, or_3_out, or_4_out, or_5_out;

  not not_1 (not_1_out, B);
  not not_2 (not_2_out, C);
  not not_3 (not_3_out, A);
  not not_4 (not_4_out, A);
  not not_5 (not_5_out, C);
  not not_6 (not_6_out, A);
  not not_7 (not_7_out, B);
  not not_8 (not_8_out, C);
  or or_1 (or_1_out, A, B, C);
  or or_2 (or_2_out, A, not_1_out, not_2_out);
  or or_3 (or_3_out, not_3_out, B, C);
  or or_4 (or_4_out, not_4_out, B, not_5_out);
  or or_5 (or_5_out, not_6_out, not_7_out, not_8_out);
  and and_1 (and_1_out, or_1_out, or_2_out, or_3_out, or_4_out, or_5_out);
  LED led_1 (.in(and_1_out));

  // Notes on the sheet:
  //   F
endmodule
