// Logisim project Lab2(min).circ as structural Verilog: 1 circuit, main circuit main
module main (
  input  in_1,
  input  in_2,
  input  in_3
);

  wire A_prime_B_prime_C_out, A_prime_BC_prime_out, ABC_prime_out, not_1_out, not_2_out, not_3_out,
       not_4_out, not_5_out, or_1_out;

  not not_1 (not_1_out, in_1);
  not not_2 (not_2_out, in_2);
  not not_3 (not_3_out, in_3);
  not not_4 (not_4_out, in_1);
  not not_5 (not_5_out, in_3);
  and A_prime_B_prime_C (A_prime_B_prime_C_out, not_1_out, not_2_out, in_3);
  and A_prime_BC_prime (A_prime_BC_prime_out, not_4_out, in_2, not_5_out);
  and ABC_prime (ABC_prime_out, in_1, in_2, not_3_out);
  or or_1 (or_1_out, A_prime_B_prime_C_out, A_prime_BC_prime_out, ABC_prime_out);
  LED led_1 (.in(or_1_out));

  // Notes on the sheet:
  //   F
endmodule
