// Logisim project Lab3(max-NOR).circ as structural Verilog: 1 circuit, main circuit main
module main (
  input  A,
  input  B,
  input  C
);

  wire nor_1_out, nor_2_out, nor_3_out, nor_4_out;

  nor nor_1 (nor_1_out, B, C);
  nor nor_2 (nor_2_out, C, C);
  nor nor_3 (nor_3_out, A, nor_2_out);
  nor nor_4 (nor_4_out, nor_1_out, nor_3_out);
  LED led_1 (.in(nor_4_out));

  // Notes on the sheet:
  //   B
  //   C
  //   A
  //   C'
  //   (B+C)'
  //   ( A+C' )'
  //   Group: 2
  //   (B+C)'
  //   F=
  //   Najifa Tabassum
  //   2211578042
  //   Experiment: 03
  //   ( A+C' )
endmodule
