// Logisim project Lab7c1.circ as structural Verilog: 1 circuit, main circuit main
module main (
  input  A_S1,
  input  B_S0,
  input  C,
  output out_4
);

  wire and_1_out, and_2_out, and_3_out, and_4_out, not_1_out, not_2_out, not_3_out, not_4_out, or_1_out,
       or_2_out;

  not not_1 (not_1_out, A_S1);
  not not_2 (not_2_out, B_S0);
  not not_3 (not_3_out, A_S1);
  not not_4 (not_4_out, B_S0);
  and and_1 (and_1_out, 1'b1, not_1_out, not_2_out);
  and and_2 (and_2_out, 1'b0, B_S0, not_3_out);
  and and_3 (and_3_out, C, A_S1, not_4_out);
  and and_4 (and_4_out, C, A_S1, B_S0);
  or or_1 (or_1_out, and_1_out, and_2_out);
  or or_2 (or_2_out, and_3_out, and_4_out);
  or or_3 (out_4, or_1_out, or_2_out);

  // Notes on the sheet:
  //   GND
  //   Vcc
endmodule
