// Logisim project Lab7c3.circ as structural Verilog: 1 circuit, main circuit main
module main (
  input  A,
  input  B,
  input  C,
  output out_4,
  output out_5,
  output out_6,
  output out_7,
  output out_8,
  output out_9,
  output out_10,
  output out_11
);

  wire n74138_1_pin4, n74138_1_pin6;

  _74138 u_74138_1 (
    .pin1(A), .pin2(B), .pin3(C), .pin4(n74138_1_pin4), .pin5(n74138_1_pin4), .pin6(n74138_1_pin6),
    .pin7(out_11), .pin15(out_4), .pin14(out_5), .pin13(out_6), .pin12(out_7), .pin11(out_8), .pin10(out_9),
    .pin9(out_10));
  // also tied to GND on the sheet: n74138_1_pin4
  // also tied to VCC on the sheet: n74138_1_pin6
endmodule
