// Logisim project Lab8J_Kflipflop.circ as structural Verilog: 1 circuit, main circuit main
module main (
  input  J,
  input  K,
  output out_3,
  output out_4
);

  wire clock_1_out;

  Clock clock_1 (.out(clock_1_out));
  J_K_Flip_Flop j_k_ff_1 (.J(J), .K(K), .clk(clock_1_out), .Q(out_3), .Qn(out_4));  // open: preset, reset
endmodule
