// Logisim project Lab8_D_T_flipflop.circ as structural Verilog: 1 circuit, main circuit main
module main (
  input  in_1,
  input  in_2,
  output out_3,
  output out_4,
  output out_5,
  output out_6
);

  wire clock_1_out, clock_2_out;

  Clock clock_1 (.out(clock_1_out));
  D_Flip_Flop d_ff_1 (.D(in_1), .clk(clock_1_out), .Q(out_3), .Qn(out_4));  // open: preset, reset
  T_Flip_Flop t_ff_1 (.T(in_2), .clk(clock_2_out), .Q(out_5), .Qn(out_6));  // open: reset, preset
  Clock clock_2 (.out(clock_2_out));

  // Notes on the sheet:
  //   D-flip-flop
endmodule
