// Logisim project Lab8_shift_registor.circ as structural Verilog: 1 circuit, main circuit main
module main (
  input  in_1,
  output Q3,
  output Q0,
  output Q1,
  output Q2
);

  wire clock_1_out;

  Clock clock_1 (.out(clock_1_out));
  _7474 u_7474_1 (
    .pin2(in_1), .pin3(clock_1_out), .pin5(Q0), .pin12(Q0), .pin11(clock_1_out), .pin9(Q1));  // open: pin1, pin4, pin6, pin13, pin10, pin8
  _7474 u_7474_2 (
    .pin2(Q1), .pin3(clock_1_out), .pin5(Q2), .pin12(Q2), .pin11(clock_1_out), .pin9(Q3));  // open: pin1, pin4, pin6, pin13, pin10, pin8
endmodule
