// Logisim project lab7c2.circ as structural Verilog: 1 circuit, main circuit main
module main (
  input  D,
  input  [2:0] A_B_C,
  output out_3
);

  Multiplexer #(.select(3)) multiplexer_1 (
    .in0(1'b1), .in1(D), .in2(D), .in3(1'b0), .in4(1'b1), .in5(1'b0), .in6(1'b0), .in7(1'b1), .out(out_3),
    .sel(A_B_C));

  // Notes on the sheet:
  //   GND
  //   Vcc
  //   A = S2
  //   B = S1
  //   C = S0
endmodule
