// Logisim project prac5.circ as structural Verilog: 1 circuit, main circuit main
module main (
  input  A1,
  input  A2,
  input  A3,
  input  A4,
  input  in_5,
  input  B1,
  input  B2,
  input  B3,
  input  B4,
  output Cout,
  output _1,
  output _2,
  output _3,
  output _4
);

  wire n74283_1_pin2, n74283_1_pin11, n74283_1_pin15, xor_1_out;

  xor xor_1 (xor_1_out, B1, in_5);
  _74283 u_74283_1 (
    .pin1(_2), .pin2(n74283_1_pin2), .pin3(A2), .pin4(_1), .pin5(A1), .pin6(xor_1_out), .pin7(in_5),
    .pin15(n74283_1_pin15), .pin14(A3), .pin13(_3), .pin12(A4), .pin11(n74283_1_pin11), .pin10(_4),
    .pin9(Cout));
  xor xor_2 (n74283_1_pin2, B2, in_5);
  xor xor_3 (n74283_1_pin15, B3, in_5);
  xor xor_4 (n74283_1_pin11, B4, in_5);

  // Notes on the sheet:
  //   Cin / M
endmodule
