// Logisim project project_D_ff.circ as structural Verilog: 2 circuits, main circuit main
module main (
  output Qc,
  output QB,
  output QA
);

  wire and_1_out, and_2_out, and_3_out, and_4_out, and_5_out, and_6_out, bcd_1_a, bcd_1_b, bcd_1_c, bcd_1_d,
       bcd_1_e, bcd_1_f, bcd_1_g, clock_1_out, DA_qn, DB_qn, DC_qn, or_1_out, or_2_out, or_3_out;

  or or_1 (or_1_out, and_2_out, and_1_out);
  Clock clock_1 (.out(clock_1_out));
  D_Flip_Flop DC (.D(or_1_out), .clk(clock_1_out), .Q(Qc), .Qn(DC_qn));  // open: preset, reset
  and and_1 (and_1_out, Qc, DB_qn);
  and and_2 (and_2_out, DC_qn, QB, QA);
  or or_2 (or_2_out, and_4_out, and_3_out);
  D_Flip_Flop DB (.D(or_2_out), .clk(clock_1_out), .Q(QB), .Qn(DB_qn));  // open: preset, reset
  and and_3 (and_3_out, DC_qn, QB, DA_qn);
  and and_4 (and_4_out, DB_qn, QA);
  BCD bcd_1 (
    .in_1(Qc), .in_2(QB), .in_3(QA), .a(bcd_1_a), .b(bcd_1_b), .c(bcd_1_c), .d(bcd_1_d), .e(bcd_1_e),
    .f(bcd_1_f), .g(bcd_1_g));
  or or_3 (or_3_out, and_6_out, and_5_out);
  D_Flip_Flop DA (.D(or_3_out), .clk(clock_1_out), .Q(QA), .Qn(DA_qn));  // open: preset, reset
  and and_5 (and_5_out, DA_qn, DB_qn);
  _7_Segment_Display u_7_segment_display_1 (
    .g(bcd_1_g), .f(bcd_1_f), .a(bcd_1_a), .b(bcd_1_b), .e(bcd_1_e), .d(bcd_1_d), .c(bcd_1_c));  // open: dp
  and and_6 (and_6_out, DA_qn, DC_qn);

  // Notes on the sheet:
  //   DC=B'C+
  //   ABC'
  //   B'C
  //   DB=AB'+A'BC'
  //   ABC'
  //   AB'
  //   A'BC'
  //   DA=A'B'+A'C'
  //   A'C'
  //   A'B'
  //   Basic gate+ D_ff
endmodule

module BCD (
  input  in_1,
  input  in_2,
  input  in_3,
  output a,
  output b,
  output c,
  output d,
  output e,
  output f,
  output g
);

  wire and_1_out, and_2_out, and_3_out, and_4_out, and_5_out, and_6_out, and_7_out, and_8_out, and_9_out,
       not_1_out, not_2_out, not_3_out;

  not not_1 (not_1_out, in_1);
  not not_2 (not_2_out, in_2);
  not not_3 (not_3_out, in_3);
  or or_1 (a, not_2_out, in_1);
  or or_2 (b, not_1_out, in_3, in_2);
  or or_3 (c, in_2, in_1);
  and and_1 (and_1_out, not_1_out, not_2_out);
  and and_2 (and_2_out, in_1, in_2);
  or or_4 (d, and_1_out, and_2_out, and_3_out);
  and and_3 (and_3_out, not_2_out, not_3_out);
  and and_4 (and_4_out, not_1_out, not_2_out);
  or or_5 (e, and_4_out, and_5_out);
  and and_5 (and_5_out, in_1, in_2);
  and and_6 (and_6_out, in_1, not_3_out);
  or or_6 (f, and_6_out, and_7_out);
  and and_7 (and_7_out, in_1, in_2);
  and and_8 (and_8_out, not_1_out, not_2_out);
  or or_7 (g, and_8_out, and_9_out);
  and and_9 (and_9_out, in_1, not_3_out);
endmodule
