// Logisim project project_T_ff.circ as structural Verilog: 2 circuits, main circuit main
module main (
  output QC,
  output QB,
  output QA
);

  wire and_1_out, and_2_out, and_3_out, and_4_out, and_5_out, bcd_1_a, bcd_1_b, bcd_1_c, bcd_1_d, bcd_1_e,
       bcd_1_f, bcd_1_g, clock_1_out, or_1_out, or_2_out, or_3_out, TA_qn, TB_qn, TC_qn;

  Clock clock_1 (.out(clock_1_out));
  or or_1 (or_1_out, and_2_out, and_1_out);
  T_Flip_Flop TC (.T(or_1_out), .clk(clock_1_out), .Q(QC), .Qn(TC_qn));  // open: reset, preset
  and and_1 (and_1_out, TC_qn, QB, QA);
  and and_2 (and_2_out, QC, QB, TA_qn);
  T_Flip_Flop TB (.T(or_3_out), .clk(clock_1_out), .Q(QB), .Qn(TB_qn));  // open: reset, preset
  or or_2 (or_2_out, TB_qn, TC_qn);
  BCD bcd_1 (
    .in_1(QC), .in_2(QB), .in_3(QA), .a(bcd_1_a), .b(bcd_1_b), .c(bcd_1_c), .d(bcd_1_d), .e(bcd_1_e),
    .f(bcd_1_f), .g(bcd_1_g));
  or or_3 (or_3_out, and_5_out, and_4_out, and_3_out);
  T_Flip_Flop TA (.T(or_2_out), .clk(clock_1_out), .Q(QA), .Qn(TA_qn));  // open: reset, preset
  and and_3 (and_3_out, TB_qn, QA);
  _7_Segment_Display u_7_segment_display_1 (
    .g(bcd_1_g), .f(bcd_1_f), .a(bcd_1_a), .b(bcd_1_b), .e(bcd_1_e), .d(bcd_1_d), .c(bcd_1_c));  // open: dp
  and and_4 (and_4_out, QA, TC_qn);
  and and_5 (and_5_out, TA_qn, QB, QC);

  // Notes on the sheet:
  //   TC=A'BC+ABC'
  //   A'BC
  //   ABC'
  //   TB=AB'+AC'+A'BC
  //   B'
  //   C'
  //   TA=B'+C'
  //   Basic gate+ T_ff
  //   A'B
  //   A'C
  //   A'BC
endmodule

module BCD (
  input  in_1,
  input  in_2,
  input  in_3,
  output a,
  output b,
  output c,
  output d,
  output e,
  output f,
  output g
);

  wire and_1_out, and_2_out, and_3_out, and_4_out, and_5_out, and_6_out, and_7_out, and_8_out, and_9_out,
       not_1_out, not_2_out, not_3_out;

  not not_1 (not_1_out, in_1);
  not not_2 (not_2_out, in_2);
  not not_3 (not_3_out, in_3);
  or or_1 (a, not_2_out, in_1);
  or or_2 (b, not_1_out, in_3, in_2);
  or or_3 (c, in_2, in_1);
  and and_1 (and_1_out, not_1_out, not_2_out);
  and and_2 (and_2_out, in_1, in_2);
  or or_4 (d, and_1_out, and_2_out, and_3_out);
  and and_3 (and_3_out, not_2_out, not_3_out);
  and and_4 (and_4_out, not_1_out, not_2_out);
  or or_5 (e, and_4_out, and_5_out);
  and and_5 (and_5_out, in_1, in_2);
  and and_6 (and_6_out, in_1, not_3_out);
  or or_6 (f, and_6_out, and_7_out);
  and and_7 (and_7_out, in_1, in_2);
  and and_8 (and_8_out, not_1_out, not_2_out);
  or or_7 (g, and_8_out, and_9_out);
  and and_9 (and_9_out, in_1, not_3_out);
endmodule
