// Logisim project project_universal.circ as structural Verilog: 3 circuits, main circuit main
module main (
  output Qc,
  output Qb,
  output Qa
);

  wire and_1_out, and_2_out, and_3_out, and_4_out, and_5_out, bcd_1_a, bcd_1_b, bcd_1_c, bcd_1_d, bcd_1_e,
       bcd_1_f, bcd_1_g, clock_1_out, JA_qn, JB_qn, JC_qn, or_1_out, or_2_out;

  and and_1 (and_1_out, Qa, Qb, JC_qn);
  J_K_Flip_Flop JC (.J(and_1_out), .K(and_2_out), .clk(clock_1_out), .Q(Qc), .Qn(JC_qn));  // open: preset, reset
  Clock clock_1 (.out(clock_1_out));
  BCD bcd_1 (
    .h(Qc), .x2(Qb), .x3(Qa), .a(bcd_1_a), .b(bcd_1_b), .c(bcd_1_c), .d(bcd_1_d), .e(bcd_1_e), .f(bcd_1_f),
    .g(bcd_1_g));
  and and_2 (and_2_out, JA_qn, Qb);
  _7_Segment_Display u_7_segment_display_1 (
    .g(bcd_1_g), .f(bcd_1_f), .a(bcd_1_a), .b(bcd_1_b), .e(bcd_1_e), .d(bcd_1_d), .c(bcd_1_c));  // open: dp
  J_K_Flip_Flop JB (.J(and_3_out), .K(or_1_out), .clk(clock_1_out), .Q(Qb), .Qn(JB_qn));  // open: preset, reset
  and and_3 (and_3_out, JB_qn, Qa);
  or or_1 (or_1_out, and_4_out, and_5_out);
  and and_4 (and_4_out, Qc, JA_qn);
  or or_2 (or_2_out, JB_qn, JC_qn);
  and and_5 (and_5_out, JC_qn, Qa);
  J_K_Flip_Flop JA (.J(or_2_out), .K(or_2_out), .clk(clock_1_out), .Q(Qa), .Qn(JA_qn));  // open: preset, reset

  // Notes on the sheet:
  //   C
  //   B
  //   A
  //   A'B
  //   ABC'
  //   AB'
  //   A'C+AC'
  //   B'+C'
  //   B'+C'
  //   Universal gate+J-K
endmodule

module BCD (
  input  h,
  input  x2,
  input  x3,
  output a,
  output b,
  output c,
  output d,
  output e,
  output f,
  output g
);

  wire nand_1_out, nand_2_out, nand_3_out, nand_7_out, nand_8_out, nand_9_out, nand_10_out, nand_11_out,
       nand_12_out, nand_13_out, nand_14_out, nand_15_out;

  nand nand_1 (nand_1_out, 1'b1, h);
  nand nand_2 (nand_2_out, 1'b1, x2);
  nand nand_3 (nand_3_out, 1'b1, x3);
  nand nand_4 (a, x2, nand_1_out);
  nand nand_5 (b, h, nand_3_out, nand_2_out);
  nand nand_6 (c, nand_2_out, nand_1_out);
  nand nand_7 (nand_7_out, nand_1_out, nand_2_out);
  nand nand_8 (nand_8_out, h, x2);
  nand nand_9 (nand_9_out, nand_2_out, nand_3_out);
  nand nand_10 (nand_10_out, nand_1_out, nand_2_out);
  nand nand_11 (nand_11_out, h, x2);
  nand nand_12 (nand_12_out, h, nand_3_out);
  nand nand_13 (nand_13_out, h, x2);
  nand nand_14 (nand_14_out, nand_1_out, nand_2_out);
  nand nand_15 (nand_15_out, h, nand_3_out);
  nand nand_16 (d, nand_7_out, nand_8_out, nand_9_out);
  nand nand_17 (e, nand_10_out, nand_11_out);
  nand nand_18 (f, nand_12_out, nand_13_out);
  nand nand_19 (g, nand_14_out, nand_15_out);
endmodule

module project (
  input  h,
  input  x2,
  input  x3,
  output a,
  output b,
  output c,
  output d,
  output e,
  output f,
  output g
);

  wire nand_1_out, nand_2_out, nand_3_out, nand_4_out, nand_5_out, nand_6_out, nand_7_out, nand_8_out,
       nand_9_out, nand_10_out, nand_11_out, nand_12_out, nand_13_out, nand_14_out, nand_15_out, nand_19_out,
       nand_20_out, nand_21_out, nand_22_out, nand_23_out, nand_24_out, nand_25_out, nand_26_out, nand_27_out;

  nand nand_1 (nand_1_out, 1'b1, h);
  nand nand_2 (nand_2_out, 1'b1, x3);
  nand nand_3 (nand_3_out, 1'b1, x2);
  nand nand_4 (nand_4_out, 1'b1, x2);
  nand nand_5 (nand_5_out, 1'b1, h);
  nand nand_6 (nand_6_out, 1'b1, h);
  nand nand_7 (nand_7_out, 1'b1, x2);
  nand nand_8 (nand_8_out, 1'b1, x2);
  nand nand_9 (nand_9_out, 1'b1, x3);
  nand nand_10 (nand_10_out, 1'b1, h);
  nand nand_11 (nand_11_out, 1'b1, x2);
  nand nand_12 (nand_12_out, 1'b1, x3);
  nand nand_13 (nand_13_out, 1'b1, h);
  nand nand_14 (nand_14_out, 1'b1, x2);
  nand nand_15 (nand_15_out, 1'b1, x3);
  nand nand_16 (a, x2, nand_1_out);
  nand nand_17 (b, h, nand_2_out, nand_3_out);
  nand nand_18 (c, nand_4_out, nand_5_out);
  nand nand_19 (nand_19_out, nand_6_out, nand_7_out);
  nand nand_20 (nand_20_out, h, x2);
  nand nand_21 (nand_21_out, nand_8_out, nand_9_out);
  nand nand_22 (nand_22_out, nand_10_out, nand_11_out);
  nand nand_23 (nand_23_out, h, x2);
  nand nand_24 (nand_24_out, h, nand_12_out);
  nand nand_25 (nand_25_out, h, x2);
  nand nand_26 (nand_26_out, nand_13_out, nand_14_out);
  nand nand_27 (nand_27_out, h, nand_15_out);
  nand nand_28 (d, nand_19_out, nand_20_out, nand_21_out);
  nand nand_29 (e, nand_22_out, nand_23_out);
  nand nand_30 (f, nand_24_out, nand_25_out);
  nand nand_31 (g, nand_26_out, nand_27_out);
endmodule
